# Fritzing sketch Arduino1010 (saved by Fritzing 0.9.2b)
circuit board: 8.46667cm x 5.64444cm
breadboards: 1

parts:
  Main_Board = Arduino Leonardo (Rev3b)
  R = Resistor [tolerance=±20% resistance=330 package=THT]
  Joystick = Thumb Joystick
  LED = smd LED [color="Green (555nm)" package="0603 [SMD]"]
  LED_2 = LED - 5mm [color="Red (633nm)" package="5 mm [THT]"]
  LED_3 = LED - 5mm [color="Red (633nm)" package="5 mm [THT]"]
  R_2 = Resistor [tolerance=±5% resistance=330 package=THT]
  R_3 = Resistor [tolerance=±5% resistance=330 package=THT]
  Switch_1 = Pushbutton [package="[THT]"]
  LED_1 = LED - 5mm [color="Red (633nm)" package="5 mm [THT]"]
  R_4 = Resistor [tolerance=±5% resistance=330 package=THT]
  R_5 = Resistor [tolerance=±5% resistance=330 package=THT]
  R_6 = Resistor [tolerance=±5% resistance=330 package=THT]
  R_7 = Resistor [tolerance=±5% resistance=330 package=THT]
  Switch_2 = Pushbutton [package="[THT]"]
  LED_2 = LED - 5mm [color="Red (633nm)" package="5 mm [THT]"]
  R_8 = Resistor [tolerance=±5% resistance=330 package=THT]
  R_9 = Resistor [tolerance=±5% resistance=330 package=THT]
  Switch_3 = Pushbutton [package="[THT]"]
  LED_3 = LED - 5mm [color="Red (633nm)" package="5 mm [THT]"]
  Switch_Restart = Pushbutton [package="[THT]"]
  R1 = Resistor [tolerance=±5% resistance=330 package=THT]

nets:
  N1: Main_Board.D1/TX, LED.anode
  N2: Main_Board.D2/SDA, LED_2.anode
  N3: Main_Board.D3_PWM/SCL, LED_3.anode
  N4: Main_Board.D4/A6, Joystick.SEL
  N5: Main_Board.D6_PWM/A7, LED_3.anode
  N6: Main_Board.D7, R_8.Pin_0, Switch_3.Pin_1, Switch_3.Pin_2
  5V: Main_Board.5V, Joystick.VCC, Switch_1.Pin_3, Switch_1.Pin_4, Switch_2.Pin_3, Switch_2.Pin_4, Switch_3.Pin_3, Switch_3.Pin_4, Switch_Restart.Pin_3, Switch_Restart.Pin_4
  GND: Main_Board.GND, R.Pin_1, Joystick.GND, R_2.Pin_1, R_3.Pin_1, R_4.Pin_1, R_5.Pin_1, R_6.Pin_1, R_7.Pin_1, R_8.Pin_1, R_9.Pin_1, R1.Pin_1
  N7: Main_Board.A0, Joystick.HORZ
  N8: Main_Board.A1, Joystick.VERT
  N9: Main_Board.D8/A8, LED_2.anode
  N10: Main_Board.D9_PWM/A9, R_6.Pin_0, Switch_2.Pin_1, Switch_2.Pin_2
  N11: Main_Board.D11_PWM, LED_1.anode
  N12: Main_Board.D12/A11, Switch_1.Pin_1, Switch_1.Pin_2, R_5.Pin_0
  N13: Main_Board.D13_PWM, Switch_Restart.Pin_1, Switch_Restart.Pin_2, R1.Pin_0
  N14: R.Pin_0, LED.cathode
  N15: LED_2.cathode, R_2.Pin_0
  N16: LED_3.cathode, R_3.Pin_0
  N17: LED_1.cathode, R_4.Pin_0
  N18: R_7.Pin_0, LED_2.cathode
  N19: R_9.Pin_0, LED_3.cathode
